# Fritzing sketch Schema (saved by Fritzing 0.9.3b)
breadboards: 1

parts:
  Componente1 = Arduino Mega 2560 (Rev3)
  J1 = Piezo Speaker
  Componente3 = Bluetooth HC-05 Macho
  R1 = Resistor [tolerance=±5% resistance=220 package=THT]
  R2 = Resistor [tolerance=±5% resistance=220 package=THT]
  R3 = Resistor [tolerance=±5% resistance=220 package=THT]
  R4 = Resistor [tolerance=±5% resistance=220 package=THT]
  Mod1 = KY-022 Infrared Receiver Module [package="Breakout board"]
  8x8_LED_Modul_mit_MAX1 = 8x8 LED Modul mit MAX7219 [package=THT]
  7_Segment_4_Digit_Display1 = 7-SEGMENT-4DIGIT common anode [part_number="5461BS - 5462BS" package=7-segment-4digit-anode]
  OLED_I2C1 = OLED 128x64 I2C Monochrome Display

nets:
  N1: Componente1.D21/SCL, OLED_I2C1.SCK
  N2: Componente1.D20/SDA, OLED_I2C1.SDA
  N3: Componente1.D13_PWM, 7_Segment_4_Digit_Display1.pin_3
  N4: Componente1.D12_PWM, 7_Segment_4_Digit_Display1.pin_5
  N5: Componente1.D11_PWM, 7_Segment_4_Digit_Display1.pin_10
  N6: Componente1.D10_PWM, 7_Segment_4_Digit_Display1.pin_1
  N7: Componente1.D9_PWM, 7_Segment_4_Digit_Display1.pin_2
  N8: Componente1.D8_PWM, 7_Segment_4_Digit_Display1.pin_4
  5V: Componente1.5V, Componente3.VCC, Mod1.Vin, 8x8_LED_Modul_mit_MAX1.VCC_Eingang, OLED_I2C1.VDD
  GND: Componente1.GND, J1.pin1, Componente3.GND, Mod1.-, 8x8_LED_Modul_mit_MAX1.GND_Eingang, OLED_I2C1.GND
  N9: Componente1.D2_PWM, R4.Pin_1
  N10: Componente1.D3_PWM, R3.Pin_1
  N11: Componente1.D4_PWM, R2.Pin_1
  N12: Componente1.D5_PWM, R1.Pin_1
  N13: Componente1.D6_PWM, 7_Segment_4_Digit_Display1.pin_11
  N14: Componente1.D7_PWM, 7_Segment_4_Digit_Display1.pin_7
  N15: Componente1.D22, Mod1.S
  N16: Componente1.D23, 8x8_LED_Modul_mit_MAX1.CS_Eingang
  N17: Componente1.D24, 8x8_LED_Modul_mit_MAX1.DIN_Eingang
  N18: Componente1.D25, 8x8_LED_Modul_mit_MAX1.CLK_Eingang
  N19: Componente1.D26, J1.pin2
  N20: Componente1.D50, Componente3.TXD
  N21: Componente1.D51, Componente3.RXD
  N22: R1.Pin_0, 7_Segment_4_Digit_Display1.pin_6
  N23: R2.Pin_0, 7_Segment_4_Digit_Display1.pin_8
  N24: R3.Pin_0, 7_Segment_4_Digit_Display1.pin_9
  N25: R4.Pin_0, 7_Segment_4_Digit_Display1.pin_12

custom parts:
  KY-022 Infrared Receiver Module: KY-022 IR receiver module, reacts to 38kHz infrared light.
  7-SEGMENT-4DIGIT common anode: A 7 Segment 4 Digit common anode display, with decimal points
