# Fritzing sketch Schema (saved by Fritzing 0.9.3b)
breadboards: 1

parts:
  Componente1 = Arduino Nano (Rev3.0) (ICSP)
  LCD1 = 1_7in tft lcd

nets:
  N1: Componente1.GND, LCD1.pin_1
  N2: Componente1.D8, LCD1.pin_5
  N3: Componente1.D9, LCD1.pin_6
  N4: Componente1.D10, LCD1.pin_7
  N5: Componente1.D11/MOSI, LCD1.pin4
  N6: Componente1.5V, LCD1.pin_8
  N7: Componente1.3V3, LCD1.pin2
  N8: Componente1.D13/SCK, LCD1.pin3

custom parts:
  1_7in tft lcd: This is the Zoll 1.77in spi lcd display. The 1.77" display has 128x160 color pixels.
